// Digital circuit cpu.dig as structural Verilog
module cpu (
  input  clk,
  output [7:0] out_2,
  output [7:0] out_3,
  output [7:0] out_4
);

  wire add_1_c_o, button_1_out, button_2_out, driver_1_out, driver_2_out, LoadA, LoadB, switchdt_1_p3;
  wire [7:0] dipswitch_3_out;

  Button button_1 (.out(button_1_out));
  DipSwitch dipswitch_1 (.out(LoadA));
  DipSwitch dipswitch_2 (.out(LoadB));
  DipSwitch dipswitch_3 (.out(dipswitch_3_out[0]));
  DipSwitch dipswitch_4 (.out(dipswitch_3_out[1]));
  DipSwitch dipswitch_5 (.out(dipswitch_3_out[2]));
  DipSwitch dipswitch_6 (.out(dipswitch_3_out[3]));
  DipSwitch dipswitch_7 (.out(dipswitch_3_out[4]));
  DipSwitch dipswitch_8 (.out(dipswitch_3_out[5]));
  DipSwitch dipswitch_9 (.out(dipswitch_3_out[6]));
  DipSwitch dipswitch_10 (.out(dipswitch_3_out[7]));
  // SwitchDT switchdt_1: pin names not known; wires that end beside it: button_1_out, clk, switchdt_1_p3, dipswitch_3_out, dipswitch_3_out
  D_FF #(.Bits(8)) d_ff_1 (.D(dipswitch_3_out), .C(driver_1_out), .Q(out_3));  // open: nQ
  assign driver_1_out = LoadA ? switchdt_1_p3 : 1'bz;  // Driver driver_1
  D_FF #(.Bits(8)) d_ff_2 (.D(dipswitch_3_out), .C(driver_2_out), .Q(out_4));  // open: nQ
  assign driver_2_out = LoadB ? switchdt_1_p3 : 1'bz;  // Driver driver_2
  Add #(.Bits(8)) add_1 (.a(out_3), .b(out_4), .c_i(button_2_out), .s(out_2), .c_o(add_1_c_o));
  Button button_2 (.out(button_2_out));
  LED led_1 (.in(add_1_c_o));

  // Notes on the sheet:
  //   Data Bus
endmodule
