// Logisim project dice.circ as structural Verilog: 1 circuit, main circuit main
module main (
  input  in_1,
  input  in_2,
  input  in_3
);

  wire and_1_out, and_2_out, clock_1_out;
  wire [1:0] counter_2_q;
  wire [2:2] counter_1_q;
  wire [3:0] counter_1_q_2;
  wire [4:0] undriven;
  wire [7:0] rom_1_data;

  Counter #(.width(5), .max('h1f)) counter_1 (
    .D(undriven), .count(undriven[0]), .Q({counter_1_q_2[3:2], counter_1_q[2], counter_1_q_2[1:0]}),
    .clk(and_1_out), .clr(and_2_out));  // open: load, carry
  and and_1 (and_1_out, in_3, clock_1_out);
  and and_2 (and_2_out, counter_1_q[2], counter_1_q_2[3]);
  Clock clock_1 (.out(clock_1_out));
  Counter #(.width(2), .max('h3)) counter_2 (.Q(counter_2_q), .clk(clock_1_out));  // open: load, D, count, carry, clr
  LED led_1 (.in(counter_1_q_2[0]));
  LED led_2 (.in(counter_1_q_2[1]));
  LED led_3 (.in(counter_1_q[2]));
  LED led_4 (.in(counter_1_q_2[2]));
  LED led_5 (.in(counter_1_q_2[3]));
  _7_Segment_Display u_7_segment_display_1 ();  // open: g, f, a, b, e, d, c, dp
  _7_Segment_Display u_7_segment_display_2 (.dp(rom_1_data[7]));  // open: g, f, a, b, e, d, c
  LED led_6 ();  // open: in
  LED led_7 ();  // open: in
  LED led_8 ();  // open: in
  LED led_9 ();  // open: in
  LED led_10 ();  // open: in
  LED led_11 ();  // open: in
  ROM rom_1 (.addr({in_2, in_1, counter_2_q, counter_1_q_2}), .data(rom_1_data));  // open: sel
  LED led_12 ();  // open: in
  LED led_13 ();  // open: in
  LED led_14 ();  // open: in
  LED led_15 ();  // open: in
  LED led_16 ();  // open: in
  LED led_17 ();  // open: in
  // Pins of 1 and 5 bits meet at undriven

  // Notes on the sheet:
  //   contents of rom_1 (hex, n*v repeats v):
  //   20*ff 43*0 ff 191*0 ff
endmodule
