// Digital circuit dice.dig as structural Verilog
module dice (
  input  clk
);

  wire and_1_out, decoder_1_out_0, decoder_1_out_1, decoder_1_out_2, not_1_out, not_2_out, switch_1_a,
       switch_1_b;
  wire [1:0] disp_select_out;
  wire [5:0] _0_35_out;
  wire [7:0] Disp_d, driver_1_out;

  Counter #(.Bits(2)) disp_select (.en(1'b1), .C(clk), .clr(switch_1_a), .out(disp_select_out));  // open: ovf
  Switch switch_1 (.A(switch_1_a), .B(switch_1_b));
  and and_1 (and_1_out, _0_35_out[2], _0_35_out[5]);
  Counter #(.Bits(6)) _0_35 (.en(1'b1), .C(switch_1_b), .clr(and_1_out), .out(_0_35_out));  // open: ovf
  ROM #(.AddrBits(8), .isProgramMemory("true"), .Bits(8)) Disp (
    .A({_0_35_out, disp_select_out}), .sel(1'b1), .D(Disp_d));
  LED led_1 (.in(disp_select_out[0]));
  LED led_2 (.in(disp_select_out[1]));
  LED led_3 (.in(_0_35_out[0]));
  LED led_4 (.in(_0_35_out[1]));
  LED led_5 (.in(_0_35_out[2]));
  LED led_6 (.in(_0_35_out[3]));
  LED led_7 (.in(switch_1_a));
  assign driver_1_out = decoder_1_out_2 ? Disp_d : 8'bz;  // Driver driver_1
  Decoder #(.Selector_Bits(2)) decoder_1 (
    .sel(disp_select_out), .out_0(decoder_1_out_0), .out_1(decoder_1_out_1), .out_2(decoder_1_out_2),
    .out_3(switch_1_a));
  LED led_8 (.in(decoder_1_out_2));
  LED led_9 (.in(decoder_1_out_1));
  LED led_10 (.in(decoder_1_out_0));
  not not_1 (not_1_out, decoder_1_out_0);
  not not_2 (not_2_out, decoder_1_out_1);
  Seven_Seg #(.commonCathode("true"), .ledPersistence("true")) seven_seg_1 (
    .a(Disp_d[3]), .b(Disp_d[2]), .c(Disp_d[1]), .d(Disp_d[0]), .e(Disp_d[4]), .f(Disp_d[5]), .g(Disp_d[6]),
    .dp(Disp_d[7]), .common(not_2_out));
  LED led_11 (.in(driver_1_out[2]));
  LED led_12 (.in(driver_1_out[3]));
  LED led_13 (.in(driver_1_out[1]));
  LED led_14 (.in(driver_1_out[1]));
  LED led_15 (.in(driver_1_out[0]));
  LED led_16 (.in(driver_1_out[3]));
  LED led_17 (.in(driver_1_out[2]));
  Seven_Seg #(.commonCathode("true"), .ledPersistence("true")) seven_seg_2 (
    .a(Disp_d[3]), .b(Disp_d[2]), .c(Disp_d[1]), .d(Disp_d[0]), .e(Disp_d[4]), .f(Disp_d[5]), .g(Disp_d[6]),
    .dp(Disp_d[7]), .common(not_1_out));
  LED led_18 (.in(driver_1_out[6]));
  LED led_19 (.in(driver_1_out[7]));
  LED led_20 (.in(driver_1_out[4]));
  LED led_21 (.in(driver_1_out[5]));
  LED led_22 (.in(driver_1_out[5]));
  LED led_23 (.in(driver_1_out[7]));
  LED led_24 (.in(driver_1_out[6]));

  // Notes on the sheet:
  //   contents of Disp (hex, n*v repeats v):
  //   5d,0,11,0,4f,0,12,0,66,0,13,0,6b,0,16,0,7b,0,17,0,e,0,1e,0,7b,7b,7b,7b,e,e,e,e,7f,
  //   7f,7f,7f,6f,6f,6f,6f,3f,3f,3f,3f,6,6,6,6,5d,5d,5d,5d,4f,4f,4f,4f,66,66,66,66,6b,6b,
  //   6b,6b,7b,7b,7b,7b,e,e,e,e,7f,7f,7f,7f,6f,6f,6f,6f,3f,3f,3f,3f,6,6,6,6,5d,5d,5d,5d,
  //   4f,4f,4f,4f,66,66,66,66,6b,6b,6b,6b,7b,7b,7b,7b,e,e,e,e,7f,7f,7f,7f,6f,6f,6f,6f,3f,
  //   3f,3f,3f,6,6,6,6,5d,5d,5d,5d,4f,4f,4f,4f,66,66,66,66,6b,6b,6b,6b,7b,7b,7b,7b,e,e,
  //   e,e,7f,7f,7f,7f,6f,6f,6f,6f,3f,3f,3f,3f,6,6,6,6,5d,5d,5d,5d,4f,4f,4f,4f,66,66,66,
  //   66,6b,6b,6b,6b,7b,7b,7b,7b,e,e,e,e,7f,7f,7f,7f,6f,6f,6f,6f,3f,3f,3f,3f,6,6,6,6,5d,
  //   5d,5d,5d,4f,4f,4f,4f,66,66,66,66,6b,6b,6b,6b,7b,7b,7b,7b,e,e,e,e,7f,7f,7f,7f,6f,6f,
  //   6f,6f,3f,3f,3f,3f,6,6,6,6,5d,5d,5d,5d,4f,4f,4f,4f
endmodule
