// Logisim project dice3.circ as structural Verilog: 1 circuit, main circuit main
module main (
);

  wire clock_1_out;
  wire [7:0] counter_1_q;

  Counter counter_1 (.Q(counter_1_q), .clk(clock_1_out));  // open: load, D, count, carry, clr
  Clock clock_1 (.out(clock_1_out));
  _7_Segment_Display u_7_segment_display_1 (
    .g(counter_1_q[4]), .f(counter_1_q[5]), .a(counter_1_q[6]), .b(counter_1_q[7]), .e(counter_1_q[0]),
    .d(counter_1_q[1]), .c(counter_1_q[2]), .dp(counter_1_q[3]));
endmodule
